# Fritzing sketch AllSensors (saved by Fritzing 0.8.7b)
breadboards: 1

parts:
  Part1 = Arduino Yun
  Part2 = Gas Sensor Breakout Board
  R1 = Photocell (LDR) [package=THT]
  T1 = LM35 Temperature Sensor [package="TO92 [THT]"]
  RHT1 = Humidity and Temperature Sensor RHT03
  Part4 = Breakout Board for Electret Microphone
  R2 = Resistor [tolerance=±5% resistance=10k package=THT]
  R3 = Resistor [tolerance=±5% resistance=10k package=THT]
  R4 = Resistor [tolerance=±5% resistance=10k package=THT]

nets:
  N1: Part1.A0, Part2.B1, R2.Pin_1
  N2: Part1.A1, R4.Pin_1
  N3: Part1.A2, T1.Vout
  N4: Part1.A3, Part4.AUD
  5V: Part1.5V, R1.pin_1, T1.+Vs, Part4.VCC, R3.Pin_1
  N5: Part1.D2, RHT1.Data-signal
  GND: Part1.GND, Part2.GND, R1.pin_0, T1.GND, RHT1.GND_2, Part4.GND, R2.Pin_0, R4.Pin_0
  N6: Part2.H1, Part2.A1
  N7: RHT1.Vcc, R3.Pin_0

custom parts:
  Arduino Yun: The new Arduino Yun is a microcontroller board based on the ATmega32u4 (datasheet) and the Atheros AR9331. The Atheros processor supports a Linux distribution based on OpenWRT named Linino. The board has built-in Ethernet and WiFi support, a USB-A port, micro-SD card slot, 20 digital input/output pins (of which 7 can be used as PWM outputs and 12 as analog inputs), a 16 MHz crystal oscillator,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
