# Fritzing sketch HumiditySensor (saved by Fritzing 0.8.7b)

parts:
  Part1 = Arduino Yun
  RHT2 = Humidity and Temperature Sensor RHT03
  R1 = Resistor [tolerance=±5% resistance=220 package=THT]

nets:
  N1: Part1.D2, RHT2.Data-signal
  N2: Part1.5V, R1.Pin_1
  N3: Part1.GND, RHT2.GND_2
  N4: RHT2.Vcc, R1.Pin_0

custom parts:
  Arduino Yun: The new Arduino Yun is a microcontroller board based on the ATmega32u4 (datasheet) and the Atheros AR9331. The Atheros processor supports a Linux distribution based on OpenWRT named Linino. The board has built-in Ethernet and WiFi support, a USB-A port, micro-SD card slot, 20 digital input/output pins (of which 7 can be used as PWM outputs and 12 as analog inputs), a 16 MHz crystal oscillator,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
