# Fritzing sketch HumiditySensorDht11 (saved by Fritzing 0.8.7b)
breadboards: 1

parts:
  RHT1 = Humidity and Temperature Sensor RHT03
  Part2 = Arduino Yun
  R1 = Resistor [tolerance=±10% resistance=10k package=THT]

nets:
  VCC: RHT1.Vcc, Part2.VIN
  N1: RHT1.GND_1, Part2.D2, R1.Pin_1
  N2: RHT1.GND_2, Part2.5V, R1.Pin_0

custom parts:
  Arduino Yun: The new Arduino Yun is a microcontroller board based on the ATmega32u4 (datasheet) and the Atheros AR9331. The Atheros processor supports a Linux distribution based on OpenWRT named Linino. The board has built-in Ethernet and WiFi support, a USB-A port, micro-SD card slot, 20 digital input/output pins (of which 7 can be used as PWM outputs and 12 as analog inputs), a 16 MHz crystal oscillator,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
