# Fritzing sketch LightSensor (saved by Fritzing 0.8.7b)
breadboards: 1

parts:
  Part1 = Arduino Yun
  R4 = Photocell (LDR) [package=THT]
  R3 = Resistor [tolerance=±5% resistance=10k package=THT]

nets:
  N1: Part1.A0, R4.pin_1, R3.Pin_1
  N2: Part1.5V, R3.Pin_0
  N3: Part1.GND, R4.pin_0

custom parts:
  Arduino Yun: The new Arduino Yun is a microcontroller board based on the ATmega32u4 (datasheet) and the Atheros AR9331. The Atheros processor supports a Linux distribution based on OpenWRT named Linino. The board has built-in Ethernet and WiFi support, a USB-A port, micro-SD card slot, 20 digital input/output pins (of which 7 can be used as PWM outputs and 12 as analog inputs), a 16 MHz crystal oscillator,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
