# Fritzing sketch NoiseSensor (saved by Fritzing 0.8.7b)

parts:
  Part1 = Arduino Yun
  Part3 = Breakout Board for Electret Microphone

nets:
  N1: Part1.A0, Part3.AUD
  5V: Part1.5V, Part3.VCC
  GND: Part1.GND, Part3.GND

custom parts:
  Arduino Yun: The new Arduino Yun is a microcontroller board based on the ATmega32u4 (datasheet) and the Atheros AR9331. The Atheros processor supports a Linux distribution based on OpenWRT named Linino. The board has built-in Ethernet and WiFi support, a USB-A port, micro-SD card slot, 20 digital input/output pins (of which 7 can be used as PWM outputs and 12 as analog inputs), a 16 MHz crystal oscillator,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
